# Fritzing sketch motor_drivers_and_encoders (saved by Fritzing 0.9.3b)

parts:
  Part1 = Arduino Mega 2560 (Rev3)
  Part2 = MD30C  # not connected
  Part3 = MD30C  # not connected
  DC_Mot_Enc1 = DC Motor with two-phase hall-encoder [part_number=VT-E-G25A-06-177E]
  DC_Mot_Enc2 = DC Motor with two-phase hall-encoder [part_number=VT-E-G25A-06-177E]

nets:
  N1: Part1.GND, DC_Mot_Enc1.pin6, DC_Mot_Enc2.pin6
  N2: Part1.D2_PWM, DC_Mot_Enc2.pin3
  N3: Part1.D3_PWM, DC_Mot_Enc1.pin3
  N4: Part1.D4_PWM, DC_Mot_Enc2.pin4
  N5: Part1.D5_PWM, DC_Mot_Enc1.pin4
  N6: Part1.5V, DC_Mot_Enc1.pin5, DC_Mot_Enc2.pin5

notes:
  Yellow - Enc A
  Green - Enc B
  Blue - +5V
  Grey - GND
  LEFT
  Right
  LEFT
  pwm-11
  dir-10
  enc A - 2
  enc B - 4
  RIGHT
  pwm-13
  dir-12
  enc A - 3
  enc B - 5
